# Fritzing sketch esp_12e_clock (saved by Fritzing 0.9.3b)
breadboards: 1

parts:
  Onderdeel1 = Real Time Clock Breakout - DS1307 [part_number=147824]
  U1 = NodeMCU V1.0
  R1 = Resistor [tolerance=±5% resistance=470 package=THT]
  Onderdeel2 = ws2812b [package="smd 2812b"]
  Onderdeel3 = ws2812b [package="smd 2812b"]

nets:
  GND: Onderdeel1.GND, U1.GND, U1.SD3, Onderdeel2.VSS, Onderdeel3.VSS
  VDD: Onderdeel1.VCC, U1.D8, U1.3V3, U1.EN, Onderdeel2.VDD, Onderdeel3.VDD
  N1: Onderdeel1.SDA, U1.D6
  N2: U1.CLK, U1.SD2
  N3: U1.SD0, R1.Pin_0
  N4: R1.Pin_1, Onderdeel2.DIN
  N5: Onderdeel2.DOUT, Onderdeel3.DIN

custom parts:
  Real Time Clock Breakout - DS1307: Two wire I2C interface; Hour : Minutes : Seconds AM/PM Day Month, Date - Year; Leap year compensation; Accurate calendar up to year 2100; DS1307 based RTC with LIR2032 battery (Battery include); 56 Bytes of Non-volatile memory available to user; Working time: 1 year
  NodeMCU V1.0: ESP8266 based NodeMCU
